# Fritzing sketch counter wiring (saved by Fritzing 0.9.3b)

parts:
  S1 = Round Pushbutton
  S2 = Round Pushbutton
  S3 = Round Pushbutton
  Grove1 = Grove 4 Digit Display
  J1 = Infrared Proximity Sensor
  Part2 = Arduino Nano (Rev3.0)
  Power_plug1 = Power plug

nets:
  N1: S1.leg0, Part2.D11/MOSI
  GND: S1.leg1, S2.leg1, S3.leg1, Grove1.GND, J1.GND, Part2.GND, Power_plug1.GND
  N2: S2.leg0, Part2.D10
  N3: S3.leg0, Part2.D9
  VCC: Grove1.VCC, Part2.5V
  N4: Grove1.DIO, Part2.D3
  N5: Grove1.CLK, Part2.D2
  N6: J1.Vout, Part2.D7
  VIN: Part2.VIN, Power_plug1.VCC

notes:
  increase
  Reset
  Decrease
  E18-D80NK
