# Fritzing sketch scale wiring (saved by Fritzing 0.9.3b)

parts:
  Part1 = Arduino Mega 2560 (Rev3)
  Part2 = MAX3232
  Grove1 = Grove 4 Digit Display

nets:
  N1: Part1.D17_PWM/RX2, Part2.RXD
  N2: Part1.D16_PWM/TX2, Part2.TXD
  GND: Part1.GND, Part2.GND, Grove1.GND
  VCC: Part1.5V, Part2.VCC, Grove1.VCC
  N3: Part1.D3_PWM, Grove1.CLK
  N4: Part1.D4_PWM, Grove1.DIO

custom parts:
  MAX3232: A random MAX3232 Breakout Board from AliExpress (RS232-TTL-Converter)
