# Fritzing sketch wiring diagram final (saved by Fritzing 0.9.3b)

parts:
  U1 = LuaNode32 / ESP32
  IR_Sensor_Switch1 = Infrared Sensor Switch
  U2 = LM2596 step down module
  Part1 = MAX3232
  decrease = Round Pushbutton
  reset = Round Pushbutton
  increase = Round Pushbutton
  counter_display = TM1637 7segment 4digit display
  scale_display = TM1637 7segment 4digit display

nets:
  N1: U1.D35, decrease.leg0
  N2: U1.D32, reset.leg0
  N3: U1.D33, increase.leg0
  N4: U1.D25, IR_Sensor_Switch1.OUT
  N5: U1.D26, counter_display.CLK
  N6: U1.D27, counter_display.DIO
  GND: U1.GND, IR_Sensor_Switch1.GND, U2.IN-, U2.OUT-, Part1.GND, decrease.leg1, reset.leg1, increase.leg1, counter_display.GND, scale_display.GND
  VIN: U1.Vin, IR_Sensor_Switch1.Vcc, U2.OUT+
  VCC: U1.3V3, Part1.VCC, counter_display.Vcc, scale_display.Vcc
  N7: U1.RX2, Part1.RXD
  N8: U1.TX2, Part1.TXD
  N9: U1.D19, scale_display.CLK
  N10: U1.D22, scale_display.DIO

custom parts:
  LuaNode32 / ESP32: ESP32 based LuaNode32
  Infrared Sensor Switch: - Working voltage: DC 5V - Working current: 10~15mA - Detecting range: 3~80cm (adjustable) - Red: VCC, Green: GND, Yellow: OUT
  LM2596 step down module: LM2596 DC-DC step down power supply module 3 A.
  MAX3232: A random MAX3232 Breakout Board from AliExpress (RS232-TTL-Converter)
